// Logisim project Lab 2.circ as structural Verilog
module Task_1 (
  input  A,
  input  A_2,
  input  B,
  input  A_3,
  input  B_2,
  input  A_4,
  input  B_3,
  output A_prime,
  output AB,
  output A_prime_B_prime___A_B,
  output A_B__prime
);

  wire nand_2_out, nand_3_out, nand_4_out, nand_5_out, nand_6_out, nand_9_out;

  nand nand_1 (A_prime, A, A);
  nand nand_2 (nand_2_out, A_2, B);
  nand nand_3 (nand_3_out, A_3, A_3);
  nand nand_4 (nand_4_out, B_2, B_2);
  nand nand_5 (nand_5_out, A_4, A_4);
  nand nand_6 (nand_6_out, B_3, B_3);
  nand nand_7 (AB, nand_2_out, nand_2_out);
  nand nand_8 (A_prime_B_prime___A_B, nand_3_out, nand_4_out);
  nand nand_9 (nand_9_out, nand_5_out, nand_6_out);
  nand nand_10 (A_B__prime, nand_9_out, nand_9_out);

  // Notes on the sheet:
  //   (AB)'
  //   A'
  //   B'
  //   A'
  //   B'
  //   (A'B')"=A+B
endmodule
